# Fritzing sketch schematic (saved by Fritzing 0.7.12b)

parts:
  Part1 = MPR121 Breakout
  RaspberryPi2 = Raspberry Pi Model B

nets:
  N1: Part1.GND, RaspberryPi2.GND_2
  VCC: Part1.VCC, RaspberryPi2.3V3
  N2: Part1.SCL, RaspberryPi2.SCL
  N3: Part1.SDA, Part1.ADD, RaspberryPi2.SDA
  N4: Part1.IRQ, RaspberryPi2.#4

notes:
  To Buttons.

custom parts:
  Raspberry Pi Model B: Raspberry Pi (Model B)
